# Fritzing sketch MIDI (saved by Fritzing 0.9.3b)

parts:
  S1 = Pushbutton [package="[THT]"]
  S2 = Pushbutton [package="[THT]"]
  S3 = Pushbutton [package="[THT]"]
  S4 = Pushbutton [package="[THT]"]
  S5 = Pushbutton [package="[THT]"]
  S6 = Pushbutton [package="[THT]"]
  S7 = Pushbutton [package="[THT]"]
  S8 = Pushbutton [package="[THT]"]
  S9 = Pushbutton [package="[THT]"]
  R1 = Rotary Potentiometer (Small) [maximum_resistance=100kΩ package=THT]  # not connected
  R2 = Rotary Potentiometer (Small) [maximum_resistance=100kΩ package=THT]
  RE1 = Rotary Encoder [package=THT]  # not connected

nets:
  N1: S1.Pin_3, S1.Pin_4, S4.Pin_3, S4.Pin_4, S7.Pin_3, S7.Pin_4, R2.leg2
  N2: S2.Pin_3, S2.Pin_4, S5.Pin_3, S5.Pin_4, S8.Pin_3
  N3: S3.Pin_3, S3.Pin_4, S6.Pin_3, S6.Pin_4, S9.Pin_3

notes:
  D14
  D16
  D4
  D5
  D8
  D9
  D10
  D7
  D6
  GROUND
  5V
  A0
  A1
  D3
  D2
